# Fritzing sketch 555 timer for House Monitor_status box (saved by Fritzing 0.7.10b)
breadboards: 1

parts:
  R1 = Resistor [tolerance=±5% resistance=6.8k package=THT]
  R2 = Resistor [tolerance=±5% resistance=33k package=THT]
  R3 = Resistor [tolerance=±5% resistance=330k package=THT]
  R4 = Resistor [tolerance=±5% resistance=22k package=THT]
  C1 = Ceramic Capacitor [capacitance=10nF package="100 mil [THT, multilayer]"]
  C2 = Electrolytic Capacitor [capacitance=10µF package="100 mil [THT, electrolytic]"]
  556 = IC, DIP package, 14 pins [chip_label=556]
  C3 = Ceramic Capacitor [capacitance=10nF package="100 mil [THT, multilayer]"]
  C4 = Ceramic Capacitor [capacitance=10nF package="100 mil [THT, multilayer]"]
  J1 = Piezo Speaker
  D1 = Rectifier Diode [part_number=1N4001 package="300 mil [THT]"]

nets:
  N1: R1.Pin_1, R2.Pin_0, 556.pin13
  N2: R2.Pin_1, C1.0, 556.pin8, 556.pin12
  N3: R3.Pin_1, R4.Pin_0, 556.pin1, D1.cathode
  N4: R4.Pin_1, C2.+, 556.pin2, 556.pin6, D1.anode
  N5: C1.1, C2.-, 556.pin7, C4.1
  N6: 556.pin3, C4.0
  N7: C3.0, J1.pin1

notes:
  R1 = 6.8K
  R2 = 33K
  C = 0.01 micro farad
  low time = 200 micro sec
  high time = 300 micro sec
  freq = 2004
  R1 = 330000
  R2 = 22000
  C = 100 mico F
  low time = 1.6
  high time = 68
