# Fritzing sketch House Monitor Status Box (saved by Fritzing 0.7.10b)
breadboards: 1

parts:
  Q1 = NPN-Transistor [package="TO92 [THT]"]
  Q2 = NPN-Transistor [package="TO92 [THT]"]
  R1 = Resistor [tolerance=±5% resistance=150 package=THT]
  LED1 = LED - 5mm [color="Red (633nm)" package="5 mm [THT]"]
  LED2 = LED - 5mm [color="Red (633nm)" package="5 mm [THT]"]
  R2 = Resistor [tolerance=±5% resistance=150 package=THT]
  R3 = Resistor [tolerance=±5% resistance=120 package=THT]
  R4 = Resistor [tolerance=±5% resistance=120 package=THT]
  Part1 = XBee Explorer Regulated
  R5 = Resistor [tolerance=±5% resistance=10k package=THT]
  S1 = Pushbutton [package="[THT]"]
  R6 = Resistor [tolerance=±5% resistance=47k package=THT]  # not connected
  R7 = Resistor [tolerance=±5% resistance=220k package=THT]
  C1 = Electrolytic Capacitor [capacitance=1µF package="100 mil [THT, electrolytic]"]
  R8 = Resistor [tolerance=±5% resistance=1k package=THT]
  R9 = Resistor [tolerance=±5% resistance=220k package=THT]
  C2 = Ceramic Capacitor [capacitance=1nF package="100 mil [THT, multilayer]"]
  J1 = Piezo Speaker
  R13 = Resistor [tolerance=±5% resistance=120 package=THT]
  556 = IC, DIP package, 14 pins [chip_label=556]
  C4 = Ceramic Capacitor [capacitance=10nF package="100 mil [THT, multilayer]"]
  D1 = Rectifier Diode [part_number=1N4148 package="300 mil [THT]"]
  C5 = Ceramic Capacitor [capacitance=10nF package="100 mil [THT, multilayer]"]  # not connected

nets (from the schematic view):
  GND: Q1.E, Q2.E, Part1.GND, S1.Pin_1, S1.Pin_2, J1.pin2
  N1: Q1.B, R3.Pin_0
  N2: Q1.C, R1.Pin_0
  N3: Q2.B, R4.Pin_0
  N4: Q2.C, R2.Pin_0
  N5: R1.Pin_1, LED1.cathode
  N6: LED1.anode, LED2.anode, Part1.5V, R5.Pin_1, R7.Pin_0, R7.Pin_1, R8.Pin_0, 556.pin1, 556.pin14, C4.1
  N7: R3.Pin_1, Part1.DIO0
  N8: R4.Pin_1, Part1.DIO1
  N9: Part1.DIO2, R13.Pin_1
  N10: Part1.DIO3, 556.pin4
  N11: Part1.DIO5, R5.Pin_0, S1.Pin_3, S1.Pin_4
  N12: C1.+, D1.cathode
  N13: R9.Pin_0, 556.pin13
  N14: R9.Pin_1, C2.1, 556.pin8, 556.pin12
  N15: J1.pin1, 556.pin9
  N16: 556.pin2, 556.pin6
  N17: 556.pin11, C4.0

notes:
  Fast side
  R9 = 220000
  R8 = 1000
  C2 = 0.001 uF
  Slow Side
  R2 = 330000
  R1 = 47000
  C = 0.0004700
  V = 5
  VD=0.6
  High = R1*C * np.log(2*V - 3 * VD/V - 3 * VD)
